# Fritzing sketch mosfet_peltier_connections (saved by Fritzing 0.9.6b)
breadboards: 1

parts:
  Part1 = Arduino Micro (Rev3)
  Q1 = MOSFET-NCHANNEL [package=to220v]
  JACK1 = 2.1mm Barrel Jack with Terminal Block
  J1 = Peltier Element
  R1 = Resistor [tolerance=±5% resistance=1k package="2512 [SMD]"]
  F1 = Fan - Ventilador [package=THT]

nets:
  N1: Part1.D11_PWM, Q1.G, R1.Pin_1
  N2: Q1.D, J1.pin1
  N3: Q1.S, JACK1.NEG, F1.GND
  N4: JACK1.POS, J1.pin2, F1.5V

custom parts:
  Fan - Ventilador: Ventilador de 2 pines, se encuentra comunmente en computadoras de escritorio
